// Logisim project 2003015.circ as structural Verilog: 7 circuits, main circuit main
module main (
  input  in_1,
  input  in_2
);

  wire and_1_out;

  and and_1 (and_1_out, in_1, in_2);
endmodule

module sub4bit (
  input  in_1,
  input  in_2,
  input  in_3,
  input  in_4,
  input  in_5,
  input  in_6,
  input  in_7,
  input  in_8,
  input  in_9,
  output out_10,
  output out_11,
  output out_12
);

  wire fulladder_1_cout, fulladder_2_cout, fulladder_3_cout, or_1_out, or_2_out, or_3_out, or_4_out, q0;

  or or_1 (or_1_out, in_9, in_1);
  fulladder fulladder_1 (.a(in_5), .b(or_1_out), .Cin(in_9), .S(q0), .Cout(fulladder_1_cout));
  or or_2 (or_2_out, in_9, in_2);
  fulladder fulladder_2 (.a(in_6), .b(or_2_out), .Cin(fulladder_1_cout), .S(out_10), .Cout(fulladder_2_cout));
  or or_3 (or_3_out, in_9, in_7);
  fulladder fulladder_3 (.a(in_8), .b(or_3_out), .Cin(fulladder_2_cout), .S(out_11), .Cout(fulladder_3_cout));
  or or_4 (or_4_out, in_9, in_3);
  fulladder fulladder_4 (.a(in_4), .b(or_4_out), .Cin(fulladder_3_cout), .S(out_12));  // open: Cout
endmodule

module fulladder (
  input  a,
  input  b,
  input  Cin,
  output S,
  output Cout
);

  wire and_1_out, and_2_out, xor_1_out;

  xor xor_1 (xor_1_out, a, b);
  xor xor_2 (S, xor_1_out, Cin);
  and and_1 (and_1_out, Cin, xor_1_out);
  and and_2 (and_2_out, a, b);
  or or_1 (Cout, and_1_out, and_2_out);
endmodule

module right_shift (
  input  [3:0] A,
  input  [1:0] Shift,
  output [3:0] O
);

  Multiplexer #(.select(2)) multiplexer_1 (.in0(A[3]), .in1(1'b0), .in2(1'b0), .in3(1'b0), .out(O[3]), .sel(Shift));
  Multiplexer #(.select(2)) multiplexer_2 (.in0(A[2]), .in1(A[3]), .in2(1'b0), .in3(1'b0), .out(O[2]), .sel(Shift));
  Multiplexer #(.select(2)) multiplexer_3 (.in0(A[1]), .in1(A[2]), .in2(A[3]), .in3(1'b0), .out(O[1]), .sel(Shift));
  Multiplexer #(.select(2)) multiplexer_4 (.in0(A[0]), .in1(A[1]), .in2(A[2]), .in3(A[3]), .out(O[0]), .sel(Shift));
endmodule

module ALU (
);

  right_shift right_shift_1 ();  // open: A, Shift, O
  sub4bit sub4bit_1 ();  // open: in_1, in_2, in_3, in_4, in_5, in_6, in_7, in_8, in_9, out_10, out_11, out_12
  and4bit and4bit_1 ();  // open: A, B, O
  not4bit not4bit_1 ();  // open: in_1, out_2
  Multiplexer #(.select(2)) multiplexer_1 ();  // open: in0, in1, in2, in3, out, sel
endmodule

module and4bit (
  input  [3:0] A,
  input  [3:0] B,
  output [3:0] O
);

  and and_1 (O[3], A[3], B[3]);
  and and_2 (O[2], A[2], B[2]);
  and and_3 (O[1], A[1], B[1]);
  and and_4 (O[0], A[0], B[0]);
endmodule

module not4bit (
  input  [3:0] in_1,
  output [3:0] out_2
);

  not not_1 (out_2[3], in_1[3]);
  not not_2 (out_2[2], in_1[2]);
  not not_3 (out_2[1], in_1[1]);
  not not_4 (out_2[0], in_1[0]);

  // Other names for the same wires on the sheet: A0 = in_1[0]; A1 = in_1[1]; A2 = in_1[2]; A3 = in_1[3];
  //   O0 = out_2[0]; O1 = out_2[1]; O2 = out_2[2]; O3 = out_2[3]
endmodule
