// Logisim project registerset.circ as structural Verilog
module One_Bit_REG (
  input  Din,
  input  SEL,
  input  CLK,
  output Dout
);

  wire multiplexer_1_out;

  Multiplexer multiplexer_1 (.in0(Dout), .in1(Din), .out(multiplexer_1_out), .sel(SEL));
  D_Flip_Flop d_ff_1 (.D(multiplexer_1_out), .clk(CLK), .Q(Dout));  // open: Qn, preset, reset
endmodule

module Four_Bit_REG (
  input  [3:0] Din,
  input  SEL,
  input  CLK,
  output [3:0] Dout
);

  One_Bit_REG one_bit_reg_1 (.Din(Din[0]), .SEL(SEL), .CLK(CLK), .Dout(Dout[0]));
  One_Bit_REG one_bit_reg_2 (.Din(Din[1]), .SEL(SEL), .CLK(CLK), .Dout(Dout[1]));
  One_Bit_REG one_bit_reg_3 (.Din(Din[2]), .SEL(SEL), .CLK(CLK), .Dout(Dout[2]));
  One_Bit_REG one_bit_reg_4 (.Din(Din[3]), .SEL(SEL), .CLK(CLK), .Dout(Dout[3]));
endmodule

// Din1
module Eight_Bit_REG_By_Four (
  input  REG_EN,
  input  [2:0] WR,
  input  [3:0] WRD,
  input  [3:0] INPUT_DATA,
  input  INPUT_EN,
  input  CLK,
  input  [2:0] RA,
  input  [2:0] RB,
  output [3:0] A,
  output [3:0] B
);

  wire RG0, RG1, RG2, RG3, RG4, RG5, RG6;
  wire [3:0] R0, R1, R2, R3, R4, R5, R6, R7;

  Decoder #(.select(3)) decoder_1 (
    .out0(RG0), .out1(RG1), .out2(RG2), .out3(RG3), .out4(RG4), .out5(RG5), .out6(RG6), .sel(WR), .en(REG_EN));  // open: out7
  Four_Bit_REG REG_1 (.Din(WRD), .SEL(RG0), .CLK(CLK), .Dout(R0));
  Four_Bit_REG REG_2 (.Din(WRD), .SEL(RG1), .CLK(CLK), .Dout(R1));
  Four_Bit_REG REG_3 (.Din(WRD), .SEL(RG2), .CLK(CLK), .Dout(R2));
  Four_Bit_REG REG_4 (.Din(WRD), .SEL(RG3), .CLK(CLK), .Dout(R3));
  Four_Bit_REG REG_5 (.Din(WRD), .SEL(RG4), .CLK(CLK), .Dout(R4));
  Four_Bit_REG STACK_REG (.Din(WRD), .SEL(RG5), .CLK(CLK), .Dout(R5));
  Four_Bit_REG OUTPUT_REG (.Din(WRD), .SEL(RG6), .CLK(CLK), .Dout(R6));
  Four_Bit_REG INPUT_REG (.Din(INPUT_DATA), .SEL(INPUT_EN), .CLK(CLK), .Dout(R7));
  Multiplexer #(.select(3), .width(4)) multiplexer_1 (
    .in0(R0), .in1(R1), .in2(R2), .in3(R3), .in4(R4), .in5(R5), .in6(R6), .in7(R7), .out(B), .sel(RA));
  Multiplexer #(.select(3), .width(4)) multiplexer_2 (
    .in0(R0), .in2(R1), .in3(R2), .in4(R3), .in5(R4), .in6(R5), .in7(R6), .out(A), .sel(RB));  // open: in1
endmodule
